# Fritzing sketch DrMoratorius-SteamPack-Breadboard (saved by Fritzing 1.0.4)
perfboards: 4

parts:
  Q3 = ULN2803 Darlington Array
  Mod3 = Raspberry Pi Pico W
  U1 = JST-XH-6A
  U2 = JST XH 5A
  U3 = JST XH 4A 2.54mm [package=THT]
  KF-3 = KF-301 Relay [package=THT]
  KF-4 = KF-301 Relay [package=THT]
  R13 = Rotary Potentiometer (Large) [maximum_resistance=80kΩ knob_status=50% power=0.5W package=THT]  # not connected
  R14 = Rotary Potentiometer (Large) [maximum_resistance=80kΩ knob_status=50% power=0.5W package=THT]  # not connected
  R15 = Resistor [tolerance=±0.25% resistance=470 package="0603 [SMD]"]
  R16 = Resistor [tolerance=±0.25% resistance=470 package="0603 [SMD]"]
  R17 = Resistor [tolerance=±0.25% resistance=4.7k package="0603 [SMD]"]
  R18 = Resistor [tolerance=±0.25% resistance=4.7k package="0603 [SMD]"]
  S4 = Taiway 100-SP-X-T1 SPDT Miniature Toggle Switch [part_number=100-SP-X-T1-0-0-B1-M2 package=THT]  # not connected
  S5 = Taiway 100-SP-X-T1 SPDT Miniature Toggle Switch [part_number=100-SP-X-T1-0-0-B1-M2 package=THT]  # not connected
  S6 = Taiway 100-SP-X-T1 SPDT Miniature Toggle Switch [part_number=100-SP-X-T1-0-0-B1-M2 package=THT]  # not connected
  S7 = Taiway 100-SP-X-T1 SPDT Miniature Toggle Switch [part_number=100-SP-X-T1-0-0-B1-M2 package=THT]  # not connected
  S8 = SWITCH-MOMENTARY-2 [package=reed_switch_plastic]
  LED8 = smd LED [color="Orange (620nm)" package="1206 [SMD]"]  # not connected
  LED9 = smd LED [color="Orange (620nm)" package="1206 [SMD]"]  # not connected
  LED10 = smd LED [color="Orange (620nm)" package="1206 [SMD]"]  # not connected
  LED11 = smd LED [color="Orange (620nm)" package="1206 [SMD]"]  # not connected
  LED12 = smd LED [color="Orange (620nm)" package="1206 [SMD]"]  # not connected
  U6 = JST XH 4A 2.54mm [package=THT]
  U7 = JST-XH-6A
  U8 = JST XH 5A
  J1 = JST XH 2A male [form="♂ (male)" package=THT]
  U9 = JST XH 3A Male [chip_label=? package=THT]
  U10 = JST XH 3A Male [chip_label=? package=THT]
  U11 = JST XH 3A Male [chip_label=? package=THT]
  U12 = JST XH 3A Male [chip_label=? package=THT]
  U13 = JST XH 3A Male [chip_label=? package=THT]
  J2 = JST XH 2A male [form="♂ (male)" package=THT]
  J3 = JST XH 2A male [form="♂ (male)" package=THT]
  J4 = JST XH 2A male [form="♂ (male)" package=THT]
  J5 = JST XH 2A male [form="♂ (male)" package=THT]
  J6 = JST XH 2A male [form="♂ (male)" package=THT]
  R19 = Resistor [tolerance=±0.25% resistance=4.7k power=0.25W package=THT]
  R20 = 12mm Trimmer Potentiometer (Large) [maximum_resistance=10kΩ knob_status=50% power=0.5W package=THT]
  R21 = 12mm Trimmer Potentiometer (Large) [maximum_resistance=10kΩ knob_status=50% power=0.5W package=THT]
  R22 = Resistor [tolerance=±5% resistance=10k package="0805 [SMD]"]
  IC2 = MCP23017 I2C I/O Expander
  J7 = JST XH 2A male [form="♂ (male)" package=THT]
  Bauteil2 = I2C level shifter bidirectional

nets:
  N1: Q3.I1, IC2.GPB7
  N2: Q3.I2, IC2.GPB6
  N3: Q3.I3, IC2.GPB5
  N4: Q3.I4, IC2.GPB4
  N5: Q3.I5, IC2.GPB3
  N6: Q3.I6, IC2.GPB2
  N7: Q3.I7, IC2.GPB1
  N8: Q3.I8, IC2.GPB0
  N9: Q3.COMMON, Mod3.pin_40, U1.pin1, KF-3.power
  GND: Q3.GND, Mod3.pin_3, Mod3.pin_8, Mod3.pin_13, Mod3.pin_18, Mod3.pin_23, Mod3.pin_28, Mod3.pin_33, Mod3.pin_38, U2.pin5, U3.pin4, KF-3.ground, KF-4.ground, S8.1, IC2.VSS, IC2.A0, IC2.A1, IC2.A2, J7.pin2, Bauteil2.GND
  N10: Q3.O5, U1.pin6
  N11: Q3.O4, U1.pin5
  N12: Q3.O3, U1.pin4
  N13: Q3.O2, U1.pin3
  N14: Q3.O1, U1.pin2
  N15: Mod3.pin_1, IC2.SDA
  N16: Mod3.pin_2, IC2.SCL
  N17: Mod3.pin_4, IC2.INTA
  N18: Mod3.pin_21, Bauteil2.LV4
  N19: Mod3.pin_22, Bauteil2.LV3
  N20: Mod3.pin_32, U3.pin3
  N21: Mod3.pin_34, U3.pin2
  N22: Mod3.pin_36, U3.pin1, R22.Pin_0, IC2.VDD, Bauteil2.LV
  N23: U2.pin1, IC2.GPA3
  N24: U2.pin2, IC2.GPA2
  N25: U2.pin3, IC2.GPA1
  N26: U2.pin4, IC2.GPA0
  N27: KF-3.signal, Bauteil2.HV3
  N28: KF-4.signal, Bauteil2.HV4
  N29: KF-4.power, Bauteil2.HV
  N30: R15.Pin_0, R21.wiper
  N31: R15.Pin_1, J3.pin1
  N32: R16.Pin_0, R20.wiper
  N33: R16.Pin_1, J2.pin1
  N34: R17.Pin_0, R18.Pin_0, U7.pin6, R20.leg2, R21.leg2
  N35: R17.Pin_1, J6.pin1
  N36: R18.Pin_1, J5.pin1
  N37: S8.2, J7.pin1
  N38: U6.pin1, U12.pin3, U13.pin3
  N39: U6.pin2, U13.pin2
  N40: U6.pin3, U12.pin2
  N41: U6.pin4, U12.pin1, U13.pin1
  N42: U7.pin1, J6.pin2
  N43: U7.pin2, J5.pin2
  N44: U7.pin3, J4.pin2
  N45: U7.pin4, J3.pin2
  N46: U7.pin5, J2.pin2
  N47: U8.pin1, U11.pin1
  N48: U8.pin2, U10.pin1
  N49: U8.pin3, U9.pin1
  N50: U8.pin4, J1.pin2
  N51: U8.pin5, J1.pin1, U9.pin2, U10.pin2, U11.pin2
  N52: J4.pin1, R19.Pin_1
  N53: R22.Pin_1, IC2.RESET

notes:
  LED
  SWITCHES
  POTI
  P1
  P2
  GND P1 P2 +3V3
  GND S1 S2 S3 S4
  +5V B1 B2 L1 L2 L3
  S1
  S2
  S3
  S4
  B1
  B2
  L1
  L2
  L3
  REED
  MCP23017 INPUTS
  GPA0 - SWITCH S1
  GPA1 - SWITCH S2
  GPA2 - SWITCH S3
  GPA3 - SWITCH S4
  GPA4 - REED CONTACT (CASE OPEN)
  GPA5 - N.C.
  GPA6 - N.C.
  GPA7 - N.C.
  GPB5 - LED L1
  GPB7 - LED B1
  GPB1 - N.C.
  MCP23017 OUTPUTS
  GPB6 - LED B2
  GPB3 - LED L3
  GPB0 - N.C.
  GPB4 - LED L2
  GPB2 - N.C.
  GPIO27 - POTI P1
  GPIO2 - INTA MCP23017
  SDA0/SCL0 - MCP23017
  GPIO28 - POTI P2
  RASPBERRY PI PICO 2 W CONNECTIONS
  RELAIS FOGGER
  RELAIS OVEN LED
  GPIO16 - RELAIS FOGGER
  GPIO17 - RELAIS OVEN LED
  CASE OPEN

custom parts:
  ULN2803 Darlington Array: ULN2803 Darlington Transistor Array with Flyback Protection
  Raspberry Pi Pico W: Raspberry Pi Pico W. Based around the RP2040 microcontroller the Pico W is a low cost microcontroller device bringing Raspberry Pi quality, cost, and easy of use to the microcontroller space. The areas marked KEEPOUT in pcb silkscreen should not have traces running through them to avoid shorts on a soldered in module!
  JST-XH-6A: JST XH 6A (2.54)
  JST XH 5A: JST XH 5A 2.54.mm
  JST XH 4A 2.54mm: 4 Pin JST XH connector
  KF-301 Relay: KF-301
  JST XH 2A male: JST XH-2A
  JST XH 3A Male: 2.54 Mm JST "XH" connector
  MCP23017 I2C I/O Expander: The MCP23017 uses two i2c pins (these can be shared with other i2c devices), and in exchange gives you 16 general purpose pins. You can set each of 16 pins to be input, output, input with a pullup or open drain. There's even the ability to get an interrupt via an external pin when any of the inputs change so you don't have to keep polling the chip.
